# Fritzing sketch RadioMarellino (saved by Fritzing 1.0.3b)
circuit board: 10.4893cm x 8.30193cm
breadboards: 1

parts:
  M1 = ESP32-S2-DevKitC-1 [part_number=ESP32-S2-DevKitC-1]
  Right = Adafruit MAX98357A I2S 3W Class D Amplifier [part_number="Adafruit #3006"]
  A2 = DD4012SA [package=THT]
  Volume = KY-040 Rotary encoder [package="Breakout board"]
  J1 = screw terminal, 2 pins
  R3 = Resistor [tolerance=±5% power=0.25W resistance=220 package=THT]
  R4 = Resistor [tolerance=±5% power=0.25W resistance=220 package=THT]
  R6 = Resistor [tolerance=±5% power=0.25W resistance=220 package=THT]
  Left = Adafruit MAX98357A I2S 3W Class D Amplifier [part_number="Adafruit #3006"]
  Sinto = KY-040 Rotary encoder [package="Breakout board"]
  C1 = Capacitor Polarized [package=panasonic_c]
  C2 = Capacitor Polarized [package=panasonic_c]

nets:
  VCC: M1.pin_1, M1.pin_2, Volume.Vcc, Sinto.Vcc
  N1: M1.pin_4, Sinto.DT
  N2: M1.pin_5, Sinto.CLK
  N3: M1.pin_15, Volume.SW
  N4: M1.pin_16, Sinto.SW
  N5: M1.pin_18, Right.DIN, Left.DIN
  N6: M1.pin_19, Right.BCLK, R6.Pin_0, Left.BCLK
  N7: M1.pin_20, Right.LRCLK, Left.LRCLK
  N8: M1.pin_21, A2.pin3, R3.Pin_1, R4.Pin_1, R6.Pin_1
  GND: M1.pin_22, M1.pin_23, M1.pin_24, M1.pin_44, Right.GND, A2.pin2, Volume.GND, J1.pin1, Left.GND, Sinto.GND, C1.-, C2.-
  N9: M1.pin_41, Volume.CLK
  N10: M1.pin_42, Volume.DT
  VIN: Right.VIN, Left.VIN, C1.+, C2.+
  N11: Right.SD_MODE, R3.Pin_0
  N12: A2.pin1, J1.pin2
  N13: R4.Pin_0, Left.SD_MODE

custom parts:
  ESP32-S2-DevKitC-1: ESP32-S2-DevKitC-1 is an entry-level development board based on ESP32-S2-SOLO (on-board PCB antenna). It is based on the ESP32 microcontroller that boasts Wifi, Bluetooth, Ethernet and Low Power support all in a single chip. (vanepp) Feb 2022: converted to ESP32-S2-DevKitC-1. This module is 44pins long (2x22) and 11 pins width.
  Adafruit MAX98357A I2S 3W Class D Amplifier: Listen to this good news - we now have an all in one digital audio amp breakout board that works incredibly well with the Raspberry Pi! If you're looking for an easy and low cost way to get you digital sound files bumpin' then the MAX08357 I2S Amp Breakout is for you. It takes standard I2S digital audio input and, not only decodes it into analog, but also amplifies it directly into a speaker.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
  DD4012SA: DD4012SA 1A DC 5V 6V 9V 12V 24V to 3.3V 5V DC-DC Step-Down Buck Converter Regulator Module Board.
  KY-040 Rotary encoder: KY-040 Rotary Encoder with switch on breakout borad from AZ Delivery
